// Logisim project ddcaprojectco1.circ as structural Verilog: 1 circuit, main circuit main
module main (
  input  A,
  input  B,
  output OUTPUT
);

  wire not_1_out;

  not not_1 (not_1_out, A);
  and and_1 (OUTPUT, not_1_out, B);

  // Notes on the sheet:
  //   INPUT A 
  //   light (LDR)
  //   1 = Bright (Day)
  //   0 = Dark (Night)
  //   INPUT B
  //   Motion sensor
  //   1= Motion Dectected
  //   0 =  Not Motion
  //   7404 
  //   (inverter) 
  //   NOT Gate 
  //   1
  //   2
  //   7408 
  //   AND Gate 
  //   Light status
  //   1 = ON 
  //   0 = OFF
endmodule
